# Fritzing sketch LedVisualizer (saved by Fritzing 0.8.7b)
breadboards: 1

parts:
  Part1 = Arduino Uno (Rev3)
  U1 = WS2812 RGB LED strip
  Part2 = Bluetooth HC-05 Macho
  R1 = Resistor [tolerance=±5% resistance=100 package=THT]
  R2 = Resistor [tolerance=±5% resistance=100 package=THT]
  R3 = Resistor [tolerance=±5% resistance=100 package=THT]

nets:
  N1: Part1.D10_PWM/SS, Part2.TXD
  N2: Part1.D11_PWM/MOSI, R1.Pin_1
  N3: Part1.D3_PWM, U1.DIN
  VCC: Part1.5V, U1.VCC, Part2.VCC
  GND: Part1.GND, U1.GND, Part2.GND, R3.Pin_0
  N4: Part2.RXD, R1.Pin_0, R2.Pin_1
  N5: R2.Pin_0, R3.Pin_1

custom parts:
  WS2812 RGB LED strip: WS2812 strip
